# Fritzing sketch controle-de-temperatura-scheme (saved by Fritzing 0.9.3b)

parts:
  Part1 = Arduino Uno (Rev3)
  Part2 = Bluetooth HM-10
  R1 = Resistor [tolerance=±5% resistance=4.7 package="2512 [SMD]"]
  T2 = LM34 Temperature Sensor [package="TO92 [THT]"]

nets:
  N1: Part1.D8, Part2.BRK
  N2: Part1.D12/MISO, Part2.STATE
  N3: Part1.D2, R1.Pin_0, T2.Vout
  N4: Part1.D6_PWM, Part2.TXD
  N5: Part1.D7, Part2.RXD
  N6: R1.Pin_1, T2.GND

notes:
  DS18B20 Left Pin is GND and Right pin in parallel with the resistor is +5V
